# Fritzing sketch flashlight (saved by Fritzing 0.9.3b)
perfboards: 2

parts:
  Nano = Arduino Nano (Rev3.0)
  R1 = Resistor [tolerance=±5% resistance=100 package="1206 [SMD]"]
  R2 = Resistor [tolerance=±5% resistance=100 package="1206 [SMD]"]
  R3 = Resistor [tolerance=±5% resistance=100 package="1206 [SMD]"]
  R4 = Resistor [tolerance=±5% resistance=330 package="1206 [SMD]"]
  R5 = Resistor [tolerance=±5% resistance=330 package="1206 [SMD]"]
  S1 = Pushbutton [package="[THT]"]
  S2 = Pushbutton [package="[THT]"]
  S3 = Pushbutton [package="[THT]"]
  R6 = Resistor [tolerance=±5% resistance=1k package="1206 [SMD]"]
  R7 = Resistor [tolerance=±5% resistance=1k package="1206 [SMD]"]  # not connected
  R8 = Resistor [tolerance=±5% resistance=1k package="1206 [SMD]"]
  R9 = Resistor [tolerance=±5% resistance=10k package="1206 [SMD]"]
  VCC1 = Battery block 9V
  J1 = Piezo Speaker
  3v_20ma_Superbright_LED = smd LED [color="White (8000K)" package="0603 [SMD]"]
  LED2 = smd LED [color="White (8000K)" package="0603 [SMD]"]
  LED3 = smd LED [color="White (8000K)" package="0603 [SMD]"]
  2v_10_ma_Fun_LED = smd LED [color="Blue (470nm)" package="0603 [SMD]"]
  LED5 = smd LED [color="Blue (470nm)" package="0603 [SMD]"]

nets:
  N1: Nano.GND, R9.Pin_0, VCC1.-
  N2: Nano.D2, R1.Pin_1
  N3: Nano.D3, R2.Pin_1
  N4: Nano.D4, R3.Pin_1
  N5: Nano.D5, R4.Pin_1
  N6: Nano.D6, R5.Pin_1
  N7: Nano.D7, J1.pin2
  N8: Nano.VIN, VCC1.+
  N9: Nano.5V, R6.Pin_1
  N10: Nano.A6, R9.Pin_1
  N11: R1.Pin_0, LED3.anode
  N12: R2.Pin_0, LED2.anode
  N13: R3.Pin_0, 3v_20ma_Superbright_LED.anode
  N14: R4.Pin_0, 2v_10_ma_Fun_LED.anode
  N15: R5.Pin_0, LED5.anode
  N16: S1.Pin_1, S1.Pin_2, S3.Pin_1, S3.Pin_2
  N17: S1.Pin_3, S1.Pin_4, R6.Pin_0
  N18: S2.Pin_1, S2.Pin_2
  N19: S2.Pin_3, S2.Pin_4, R8.Pin_0
  N20: S3.Pin_3, S3.Pin_4, R8.Pin_1
